// Digital circuit EP-aula9.dig as structural Verilog
module EP_aula9 (
  input  C,
  input  C_2,
  input  D,
  input  B,
  input  A,
  input  B_2,
  input  C_3,
  input  D_2,
  input  A_2,
  input  B_3,
  input  C_4,
  input  D_3,
  output out_1,
  output out_6,
  output out_11,
  output out_16
);

  wire and_1_out, and_2_out, and_3_out, and_4_out, and_5_out, and_6_out, and_7_out, and_8_out, and_9_out,
       and_10_out, and_11_out;

  and and_1 (and_1_out, D, C_2, ~B);  // And
  and and_2 (and_2_out, B, ~D);  // And
  and and_3 (and_3_out, B, ~C_2);  // And
  or or_1 (out_6, and_1_out, and_3_out, and_2_out);
  and and_4 (and_4_out, ~A, B_2, D_2);  // And
  and and_5 (and_5_out, A_2, B_3);
  and and_6 (and_6_out, A_2, D_3);
  and and_7 (and_7_out, ~A, B_2, C_3);  // And
  and and_8 (and_8_out, A, ~B_2);  // And
  and and_9 (and_9_out, A_2, C_4);
  and and_10 (and_10_out, ~A_2, ~B_3, ~C_4, ~D_3);  // And
  and and_11 (and_11_out, ~D_2, ~C_3, A);  // And
  or or_2 (out_16, and_5_out, and_10_out, and_9_out, and_6_out);
  or or_3 (out_11, and_11_out, and_7_out, and_4_out, and_8_out);

  assign out_1 = C;

  // Notes on the sheet:
  //   Primeiro Algarismo
  //   Segundo algarismo
  //   Terceiro algarismo
  //   Quarto Algarismo
endmodule
