// Digital circuit solucao.dig as structural Verilog
module solucao (
  input  INTD,
  input  INTC,
  input  INTB,
  input  INTA,
  input  M,
  input  SA,
  input  SB,
  input  SC,
  input  SD,
  output Y
);

  wire and_1_out, multiplexer_2_out, multiplexer_3_out, multiplexer_4_out, or_1_out, or_2_out;

  Multiplexer multiplexer_1 (.sel(M), .in_0(INTA), .in_1(multiplexer_4_out), .out(Y));
  Multiplexer multiplexer_2 (.sel(or_1_out), .in_0(INTA), .in_1(INTB), .out(multiplexer_2_out));
  Multiplexer multiplexer_3 (.sel(or_1_out), .in_0(INTC), .in_1(INTD), .out(multiplexer_3_out));
  and and_1 (and_1_out, SB, ~SC);  // And
  Multiplexer multiplexer_4 (
    .sel(or_2_out), .in_0(multiplexer_2_out), .in_1(multiplexer_3_out), .out(multiplexer_4_out));
  or or_1 (or_1_out, and_1_out, SD);
  or or_2 (or_2_out, SC, SD);
endmodule
