// Digital circuit Bit-Sliced Comparator Module.dig as structural Verilog
module Bit_Sliced_Comparator_Module (
  input  A_n_1,
  input  B_n_1,
  input  A_n_eq_B_n,
  input  A_n_eq_B_n_2,
  input  A_n_eq_B_n_3,
  input  A_n_gt_B_n,
  input  A_n_lt_B_n,
  output A_n_1_gt_B_n_1,
  output A_n_1_eq_B_n_1,
  output A_n_1_lt_B_n_1
);

  wire and_1_out, and_2_out, and_3_out, and_4_out, nor_1_out, not_1_out, not_2_out;

  not not_1 (not_1_out, A_n_1);
  not not_2 (not_2_out, B_n_1);
  and and_1 (and_1_out, A_n_1, not_2_out);
  and and_2 (and_2_out, B_n_1, not_1_out);
  and and_3 (and_3_out, A_n_eq_B_n, and_1_out);
  nor nor_1 (nor_1_out, and_1_out, and_2_out);
  and and_4 (and_4_out, and_2_out, A_n_eq_B_n_2);
  or or_1 (A_n_1_gt_B_n_1, and_3_out, A_n_gt_B_n);
  and and_5 (A_n_1_eq_B_n_1, A_n_eq_B_n_3, nor_1_out);
  or or_2 (A_n_1_lt_B_n_1, and_4_out, A_n_lt_B_n);
endmodule
