// Digital circuit all_in.dig as structural Verilog
module all_in (
  input  D,
  input  C,
  output Q_d,
  output Qfd,
  output Qft
);

  my_latch_D my_latch_d_1 (.D(D), .clk(C), .Q(Q_d));  // open: Q_2
  my_flip_flop_D my_flip_flop_d_1 (.D(D), .clk(C), .Q(Qfd));
  my_toggle my_toggle_1 (.T(D), .clk(C), .Q(Qft));
endmodule
