// Digital circuit my_flip_flop_D.dig as structural Verilog
module my_flip_flop_D (
  input  D,
  input  clk,
  output Q
);

  wire my_latch_d_1_q, not_1_out;

  not not_1 (not_1_out, clk);
  my_latch_D my_latch_d_1 (.D(D), .clk(not_1_out), .Q(my_latch_d_1_q));  // open: Q_2
  my_latch_D my_latch_d_2 (.D(my_latch_d_1_q), .clk(clk), .Q(Q));  // open: Q_2
endmodule
