// Digital circuit my_latch_D.dig as structural Verilog
module my_latch_D (
  input  D,
  input  clk,
  output Q,
  output Q_2
);

  wire nand_1_out, not_1_out, or_1_out;

  not not_1 (not_1_out, D);
  nand nand_1 (nand_1_out, D, clk);
  or or_1 (or_1_out, ~not_1_out, ~clk);  // Or
  nand nand_2 (Q, nand_1_out, Q_2);
  nand nand_3 (Q_2, Q, or_1_out);
endmodule
