// Digital circuit my_toggle.dig as structural Verilog
module my_toggle (
  input  T,
  input  clk,
  output Q
);

  wire multiplexer_1_out, not_1_out;

  not not_1 (not_1_out, Q);
  Multiplexer multiplexer_1 (.sel(T), .in_0(Q), .in_1(not_1_out), .out(multiplexer_1_out));
  my_flip_flop_D my_flip_flop_d_1 (.D(multiplexer_1_out), .clk(clk), .Q(Q));
endmodule
