// Digital circuit contador.dig as structural Verilog
module contador (
  input  up,
  input  clk,
  input  enable,
  output [3:0] out_1
);

  wire multiplexer_1_out, multiplexer_2_out, multiplexer_3_out, t_ff_1_nq, t_ff_2_nq, t_ff_3_nq;

  T_FF t_ff_1 (.T(enable), .C(clk), .Q(out_1[0]), .nQ(t_ff_1_nq));
  Multiplexer multiplexer_1 (.sel(up), .in_0(out_1[0]), .in_1(t_ff_1_nq), .out(multiplexer_1_out));
  T_FF t_ff_2 (.T(enable), .C(multiplexer_1_out), .Q(out_1[1]), .nQ(t_ff_2_nq));
  Multiplexer multiplexer_2 (.sel(up), .in_0(out_1[1]), .in_1(t_ff_2_nq), .out(multiplexer_2_out));
  T_FF t_ff_3 (.T(enable), .C(multiplexer_2_out), .Q(out_1[2]), .nQ(t_ff_3_nq));
  Multiplexer multiplexer_3 (.sel(up), .in_0(out_1[2]), .in_1(t_ff_3_nq), .out(multiplexer_3_out));
  T_FF t_ff_4 (.T(enable), .C(multiplexer_3_out), .Q(out_1[3]));  // open: nQ
endmodule
