// Digital circuit reg.dig as structural Verilog
module \reg  (
  input  load,
  input  shift,
  input  esquerda,
  input  serial,
  input  [3:0] EP
);

  wire d_ff_1_q, d_ff_2_q, d_ff_3_q, d_ff_4_q;

  Multiplexer #(.Bits(2)) multiplexer_1 ();  // open: sel, in_0, in_1, out
  Multiplexer #(.Bits(4)) multiplexer_2 ();  // open: sel, in_0, in_1, out
  Multiplexer multiplexer_3 (.sel(load), .in_1(EP[0]));  // open: in_0, out
  D_FF d_ff_1 (.Q(d_ff_1_q));  // open: D, C, nQ
  Multiplexer #(.Selector_Bits(2), .Bits(4)) multiplexer_4 ();  // open: sel, in_0, in_1, in_2, in_3, out
  D_FF d_ff_2 (.Q(d_ff_2_q));  // open: D, C, nQ
  Multiplexer #(.Selector_Bits(2), .Bits(4)) multiplexer_5 ();  // open: sel, in_0, in_1, in_2, in_3, out
  D_FF d_ff_3 (.Q(d_ff_3_q));  // open: D, C, nQ
  Multiplexer #(.Selector_Bits(2), .Bits(4)) multiplexer_6 ();  // open: sel, in_0, in_1, in_2, in_3, out
  D_FF d_ff_4 (.Q(d_ff_4_q));  // open: D, C, nQ
  // Pins of 1 and 4 bits meet at EP
endmodule
