// Digital circuit zombie.dig as structural Verilog
module zombie (
  input  E0,
  input  E1,
  input  clk,
  output z
);

  wire and_2_out, and_3_out, and_4_out, and_5_out, and_6_out, and_7_out, and_8_out, and_9_out, and_10_out,
       and_11_out, and_12_out, FF0_q, FF1_q, FF2_q, or_1_out, or_2_out, or_3_out, or_4_out;

  and and_1 (z, ~E0, or_1_out);  // And
  and and_2 (and_2_out, E1, FF0_q, ~FF1_q);  // And
  and and_3 (and_3_out, ~E0, E1, ~FF1_q, FF2_q);  // And
  and and_4 (and_4_out, ~E0, ~E1, ~FF1_q);  // And
  and and_5 (and_5_out, ~E0, ~E1, ~FF0_q);  // And
  and and_6 (and_6_out, ~E0, ~FF0_q, FF1_q, ~FF2_q);  // And
  and and_7 (and_7_out, E0, ~E1, ~FF0_q, ~FF1_q, FF2_q);  // And
  and and_8 (and_8_out, E1, ~FF1_q, FF2_q);  // And
  and and_9 (and_9_out, ~E0, E1, ~FF0_q, FF1_q, ~FF2_q);  // And
  and and_10 (and_10_out, E0, ~E1, FF0_q, ~FF1_q, ~FF2_q);  // And
  and and_11 (and_11_out, E0, ~E1, ~FF0_q, FF1_q, FF2_q);  // And
  or or_1 (or_1_out, and_2_out, and_8_out);
  or or_2 (or_2_out, and_9_out, and_10_out, and_11_out);
  or or_3 (or_3_out, and_4_out, and_5_out, and_6_out, and_7_out);
  and and_12 (and_12_out, E0, ~E1, ~FF0_q, ~FF1_q, FF2_q);  // And
  D_FF FF0 (.D(or_2_out), .C(clk), .Q(FF0_q));  // open: nQ
  D_FF FF1 (.D(or_4_out), .C(clk), .Q(FF1_q));  // open: nQ
  D_FF FF2 (.D(or_3_out), .C(clk), .Q(FF2_q));  // open: nQ
  or or_4 (or_4_out, and_3_out, and_12_out);
endmodule
